// Logisim project HW2-example.circ as structural Verilog: 2 circuits, main circuit main
module main (
  input  s3,
  input  s2,
  input  s1
);

  wire and_1_out, or_1_out;

  and and_1 (and_1_out, s3, s2);
  or or_1 (or_1_out, s2, s1);
  _7_Segment_Display u_7_segment_display_1 (.g(or_1_out), .b(and_1_out));  // open: f, a, e, d, c, dp
endmodule

module seg (
  input  C,
  input  B,
  input  A,
  output a_2,
  output b_2,
  output c_2,
  output d,
  output e,
  output f,
  output g
);

  wire and_1_out, and_2_out, and_3_out, and_4_out, and_5_out, not_1_out, not_2_out, not_3_out, not_4_out,
       not_5_out, not_6_out, not_7_out, not_8_out, not_9_out, not_10_out, not_11_out, not_12_out, not_13_out;

  not not_1 (not_1_out, B);
  not not_2 (not_2_out, A);
  not not_3 (not_3_out, C);
  not not_4 (not_4_out, A);
  not not_5 (not_5_out, B);
  not not_6 (not_6_out, A);
  not not_7 (not_7_out, B);
  not not_8 (not_8_out, A);
  not not_9 (not_9_out, A);
  not not_10 (not_10_out, B);
  not not_11 (not_11_out, A);
  or or_1 (a_2, not_1_out, not_2_out, C);
  not not_12 (not_12_out, B);
  and and_1 (and_1_out, not_3_out, A);
  and and_2 (and_2_out, C, not_4_out);
  or or_2 (d, not_5_out, not_6_out, C);
  and and_3 (and_3_out, not_7_out, not_8_out);
  or or_3 (f, not_9_out, B, C);
  not not_13 (not_13_out, C);
  and and_4 (and_4_out, not_10_out, not_11_out);
  and and_5 (and_5_out, B, A);
  or or_4 (b_2, not_12_out, and_1_out, and_2_out);
  or or_5 (e, and_3_out, C);
  or or_6 (g, not_13_out, and_4_out, and_5_out);

  assign c_2 = 1'b1;
endmodule
