// Logisim project HW-2-Submission-Copy.circ as structural Verilog: 1 circuit, main circuit main
module main (
  input  i0,
  input  i1,
  input  i2
);

  wire and_1_out, and_2_out, and_3_out, and_4_out, and_5_out, nand_1_out, not_1_out, not_2_out, not_3_out,
       not_4_out, not_5_out, not_6_out, not_7_out, not_8_out, not_9_out, or_1_out, or_2_out, or_3_out,
       or_4_out, or_5_out;

  not not_1 (not_1_out, i0);
  not not_2 (not_2_out, i2);
  not not_3 (not_3_out, i1);
  and and_1 (and_1_out, not_1_out, i1, not_2_out);
  or or_1 (or_1_out, i0, not_3_out);
  and and_2 (and_2_out, or_1_out, i2);
  not not_4 (not_4_out, i1);
  not not_5 (not_5_out, i2);
  not not_6 (not_6_out, i0);
  not not_7 (not_7_out, i1);
  and and_3 (and_3_out, not_4_out, not_5_out);
  and and_4 (and_4_out, not_6_out, not_7_out);
  and and_5 (and_5_out, i0, i1);
  or or_2 (or_2_out, and_1_out, and_2_out);
  not not_8 (not_8_out, i1);
  not not_9 (not_9_out, i2);
  or or_3 (or_3_out, and_3_out, and_4_out, and_5_out);
  or or_4 (or_4_out, and_3_out, and_5_out);
  nand nand_1 (nand_1_out, i0, i1, i2);
  or or_5 (or_5_out, i0, not_8_out, not_9_out);
  _7_Segment_Display u_7_segment_display_1 (
    .g(or_2_out), .f(or_3_out), .a(1'b1), .b(nand_1_out), .e(or_4_out), .d(or_5_out), .c(1'b1));  // open: dp

  // Notes on the sheet:
  //   6 0 3 0 7 3 9 0
  //   used power source here as these segments are always on
endmodule
